// Logisim project stack_logisim_normal.circ as structural Verilog: 22 circuits, main circuit main
module main (
  input  CLK,
  input  RESET,
  input  [1:0] COMMAND,
  input  [2:0] INDEX,
  input  [3:0] IO_DATA_in,
  output [3:0] IO_DATA_out
);

  stack stack_1 (
    .CLK(CLK), .RESET(RESET), .COMMAND(COMMAND), .INDEX(INDEX), .IO_DATA_in(IO_DATA_in),
    .IO_DATA_out(IO_DATA_out));
endmodule

module stack (
  input  CLK,
  input  RESET,
  input  [1:0] COMMAND,
  input  [2:0] INDEX,
  input  [3:0] IO_DATA_in,
  output [3:0] IO_DATA_out
);

  wire not_1_out, transmission_1_p3, transmission_1_p4;
  wire [3:0] transmission_1_p2;

  not not_1 (not_1_out, COMMAND[1]);
  // Transmission_Gate #(.width(4)) transmission_1: pin names not known; wires that end beside it: COMMAND[0], transmission_1_p2, transmission_1_p3, transmission_1_p4, IO_DATA_in
  not not_2 (transmission_1_p4, transmission_1_p3);
  and and_1 (transmission_1_p3, COMMAND[0], not_1_out);
  my_stack my_stack_1 (
    .I_DATA(IO_DATA_in), .RESET(RESET), .CLK(CLK), .COMMAND(COMMAND), .INDEX(INDEX),
    .O_DATA(transmission_1_p2));

  assign IO_DATA_out = IO_DATA_in;

  // Notes on the sheet:
  //   your circuit must be here
endmodule

module rs (
  input  R,
  input  S,
  input  RESET,
  output Q,
  output INV_Q
);

  wire nor_2_out;

  nor nor_1 (Q, R, INV_Q);
  nor nor_2 (nor_2_out, Q, S);
  or or_1 (INV_Q, nor_2_out, RESET);
endmodule

module synchronized_rs (
  input  R,
  input  CLK,
  input  S,
  input  RESET,
  output Q,
  output INV_Q
);

  wire and_1_out, and_2_out;

  and and_1 (and_1_out, R, CLK);
  and and_2 (and_2_out, CLK, S);
  rs rs_1 (.R(and_1_out), .S(and_2_out), .RESET(RESET), .Q(Q), .INV_Q(INV_Q));
endmodule

module d_trigger (
  input  CLK,
  input  D,
  input  RESET,
  output Q,
  output INV_Q
);

  wire not_1_out;

  not not_1 (not_1_out, D);
  synchronized_rs synchronized_rs_1 (.R(not_1_out), .CLK(CLK), .S(D), .RESET(RESET), .Q(Q), .INV_Q(INV_Q));
endmodule

module new_and (
  input  [3:0] I_DATA,
  input  KEY,
  output [3:0] RESULT
);

  and and_1 (RESULT[0], I_DATA[0], KEY);
  and and_2 (RESULT[1], I_DATA[1], KEY);
  and and_3 (RESULT[2], I_DATA[2], KEY);
  and and_4 (RESULT[3], I_DATA[3], KEY);
endmodule

module result (
  input  [3:0] A0,
  input  [3:0] A1,
  input  [3:0] A2,
  input  [3:0] A3,
  input  [3:0] A4,
  output [3:0] res
);

  or or_1 (res[0], A0[0], A3[0], A1[0], A4[0], A2[0]);
  or or_2 (res[1], A0[1], A3[1], A1[1], A4[1], A2[1]);
  or or_3 (res[2], A0[2], A3[2], A1[2], A4[2], A2[2]);
  or or_4 (res[3], A0[3], A3[3], A1[3], A4[3], A2[3]);
endmodule

module converter (
  input  [2:0] ELEMENT_1,
  input  [2:0] ELEMENT_2,
  output [2:0] O_DATA
);

  wire and_1_out, and_2_out, and_3_out, and_4_out, and_5_out, and_6_out, and_7_out, and_8_out, and_9_out,
       and_10_out, and_11_out, and_12_out, and_13_out, and_14_out, and_15_out, and_16_out, and_17_out,
       and_18_out, and_19_out, and_20_out, and_21_out, and_22_out, and_23_out, and_24_out, and_25_out,
       and_26_out, and_27_out, and_28_out, and_29_out, and_30_out, and_31_out, and_32_out, and_33_out,
       and_34_out, and_35_out, and_36_out, and_37_out, and_38_out, and_39_out, and_40_out, check_0_1_o_data,
       check_0_2_o_data, check_1_1_o_data, check_1_2_o_data, check_2_1_o_data, check_2_2_o_data,
       check_3_1_o_data, check_3_2_o_data, check_4_1_o_data, check_4_2_o_data, not_1_out, not_2_out,
       not_3_out, not_4_out, not_5_out, not_6_out, not_7_out, not_8_out, not_9_out, not_10_out, or_1_out,
       or_2_out, or_3_out, or_4_out, or_5_out;

  check_0 check_0_1 (.I_DATA(ELEMENT_1), .O_DATA(check_0_1_o_data));
  check_1 check_1_1 (.I_DATA(ELEMENT_1), .O_DATA(check_1_1_o_data));
  check_2 check_2_1 (.I_DATA(ELEMENT_1), .O_DATA(check_2_1_o_data));
  check_3 check_3_1 (.I_DATA(ELEMENT_1), .O_DATA(check_3_1_o_data));
  check_4 check_4_1 (.I_DATA(ELEMENT_1), .O_DATA(check_4_1_o_data));
  check_0 check_0_2 (.I_DATA(ELEMENT_2), .O_DATA(check_0_2_o_data));
  check_1 check_1_2 (.I_DATA(ELEMENT_2), .O_DATA(check_1_2_o_data));
  check_2 check_2_2 (.I_DATA(ELEMENT_2), .O_DATA(check_2_2_o_data));
  check_3 check_3_2 (.I_DATA(ELEMENT_2), .O_DATA(check_3_2_o_data));
  check_4 check_4_2 (.I_DATA(ELEMENT_2), .O_DATA(check_4_2_o_data));
  and and_1 (and_1_out, check_0_1_o_data, check_0_2_o_data);
  and and_2 (and_2_out, check_0_1_o_data, check_1_2_o_data);
  and and_3 (and_3_out, check_0_1_o_data, check_2_2_o_data);
  and and_4 (and_4_out, check_0_1_o_data, check_3_2_o_data);
  and and_5 (and_5_out, check_0_1_o_data, check_4_2_o_data);
  and and_6 (and_6_out, check_1_1_o_data, check_0_2_o_data);
  and and_7 (and_7_out, check_1_1_o_data, check_1_2_o_data);
  and and_8 (and_8_out, check_1_1_o_data, check_2_2_o_data);
  and and_9 (and_9_out, check_1_1_o_data, check_3_2_o_data);
  and and_10 (and_10_out, check_1_1_o_data, check_4_2_o_data);
  and and_11 (and_11_out, check_2_1_o_data, check_0_2_o_data);
  and and_12 (and_12_out, check_2_1_o_data, check_1_2_o_data);
  and and_13 (and_13_out, check_2_1_o_data, check_2_2_o_data);
  and and_14 (and_14_out, check_2_1_o_data, check_3_2_o_data);
  and and_15 (and_15_out, check_2_1_o_data, check_4_2_o_data);
  and and_16 (and_16_out, check_3_1_o_data, check_0_2_o_data);
  and and_17 (and_17_out, check_3_1_o_data, check_1_2_o_data);
  and and_18 (and_18_out, check_3_1_o_data, check_2_2_o_data);
  and and_19 (and_19_out, check_3_1_o_data, check_3_2_o_data);
  and and_20 (and_20_out, check_3_1_o_data, check_4_2_o_data);
  and and_21 (and_21_out, check_4_1_o_data, check_0_2_o_data);
  and and_22 (and_22_out, check_4_1_o_data, check_1_2_o_data);
  and and_23 (and_23_out, check_4_1_o_data, check_2_2_o_data);
  and and_24 (and_24_out, check_4_1_o_data, check_3_2_o_data);
  and and_25 (and_25_out, check_4_1_o_data, check_4_2_o_data);
  or or_1 (or_1_out, and_1_out, and_7_out, and_13_out, and_19_out, and_25_out);
  or or_2 (or_2_out, and_5_out, and_6_out, and_12_out, and_18_out, and_24_out);
  or or_3 (or_3_out, and_4_out, and_10_out, and_11_out, and_17_out, and_23_out);
  or or_4 (or_4_out, and_3_out, and_9_out, and_15_out, and_16_out, and_22_out);
  or or_5 (or_5_out, and_14_out, and_21_out, and_20_out, and_2_out, and_8_out);
  not not_1 (not_1_out, 1'b1);
  not not_2 (not_2_out, 1'b1);
  not not_3 (not_3_out, 1'b1);
  not not_4 (not_4_out, 1'b1);
  not not_5 (not_5_out, 1'b1);
  not not_6 (not_6_out, 1'b1);
  not not_7 (not_7_out, 1'b1);
  not not_8 (not_8_out, 1'b1);
  not not_9 (not_9_out, 1'b1);
  not not_10 (not_10_out, 1'b1);
  and and_26 (and_26_out, not_1_out, or_1_out);
  and and_27 (and_27_out, not_2_out, or_1_out);
  and and_28 (and_28_out, not_3_out, or_1_out);
  and and_29 (and_29_out, 1'b1, or_2_out);
  and and_30 (and_30_out, not_4_out, or_2_out);
  and and_31 (and_31_out, not_5_out, or_2_out);
  and and_32 (and_32_out, not_6_out, or_3_out);
  and and_33 (and_33_out, 1'b1, or_3_out);
  and and_34 (and_34_out, not_7_out, or_3_out);
  and and_35 (and_35_out, 1'b1, or_4_out);
  and and_36 (and_36_out, 1'b1, or_4_out);
  and and_37 (and_37_out, not_8_out, or_4_out);
  and and_38 (and_38_out, not_9_out, or_5_out);
  and and_39 (and_39_out, not_10_out, or_5_out);
  and and_40 (and_40_out, 1'b1, or_5_out);
  or or_6 (O_DATA[0], and_26_out, and_29_out, and_32_out, and_35_out, and_38_out);
  or or_7 (O_DATA[1], and_27_out, and_33_out, and_30_out, and_36_out, and_39_out);
  or or_8 (O_DATA[2], and_28_out, and_31_out, and_34_out, and_37_out, and_40_out);
endmodule

module check_0 (
  input  [2:0] I_DATA,
  output O_DATA
);

  wire not_1_out, not_2_out, not_3_out;

  not not_1 (not_1_out, I_DATA[0]);
  not not_2 (not_2_out, I_DATA[1]);
  not not_3 (not_3_out, I_DATA[2]);
  and and_1 (O_DATA, not_1_out, not_2_out, not_3_out);
endmodule

module check_1 (
  input  [2:0] I_DATA,
  output O_DATA
);

  wire not_1_out, not_2_out;

  not not_1 (not_1_out, I_DATA[1]);
  not not_2 (not_2_out, I_DATA[2]);
  and and_1 (O_DATA, I_DATA[0], not_1_out, not_2_out);
endmodule

module check_2 (
  input  [2:0] I_DATA,
  output O_DATA
);

  wire not_1_out, not_2_out;

  not not_1 (not_1_out, I_DATA[0]);
  not not_2 (not_2_out, I_DATA[2]);
  and and_1 (O_DATA, not_1_out, I_DATA[1], not_2_out);
endmodule

module check_3 (
  input  [2:0] I_DATA,
  output O_DATA
);

  wire not_1_out;

  not not_1 (not_1_out, I_DATA[2]);
  and and_1 (O_DATA, I_DATA[0], I_DATA[1], not_1_out);
endmodule

module check_4 (
  input  [2:0] I_DATA,
  output O_DATA
);

  wire not_1_out, not_2_out;

  not not_1 (not_1_out, I_DATA[0]);
  not not_2 (not_2_out, I_DATA[1]);
  and and_1 (O_DATA, not_1_out, not_2_out, I_DATA[2]);
endmodule

module rs_modified (
  input  R,
  input  S,
  input  RESET,
  output Q,
  output INV_Q
);

  wire nor_1_out;

  nor nor_1 (nor_1_out, R, INV_Q);
  nor nor_2 (INV_Q, Q, S);
  or or_1 (Q, nor_1_out, RESET);
endmodule

module mem_4_bits (
  input  RESET,
  input  CLK,
  input  KEY,
  input  [3:0] I_DATA,
  output [3:0] O_DATA
);

  wire and_1_out;

  and and_1 (and_1_out, CLK, KEY);
  d_trigger d_trigger_1 (.CLK(and_1_out), .D(I_DATA[0]), .RESET(RESET), .Q(O_DATA[0]));  // open: INV_Q
  d_trigger d_trigger_2 (.CLK(and_1_out), .D(I_DATA[1]), .RESET(RESET), .Q(O_DATA[1]));  // open: INV_Q
  d_trigger d_trigger_3 (.CLK(and_1_out), .D(I_DATA[2]), .RESET(RESET), .Q(O_DATA[2]));  // open: INV_Q
  d_trigger d_trigger_4 (.CLK(and_1_out), .D(I_DATA[3]), .RESET(RESET), .Q(O_DATA[3]));  // open: INV_Q
endmodule

module synchronized_rs_modified (
  input  R,
  input  CLK,
  input  S,
  input  RESET,
  output Q,
  output INV_Q
);

  wire and_1_out, and_2_out;

  and and_1 (and_1_out, R, CLK);
  and and_2 (and_2_out, CLK, S);
  rs_modified rs_modified_1 (.R(and_1_out), .S(and_2_out), .RESET(RESET), .Q(Q), .INV_Q(INV_Q));
endmodule

module jk_trigger (
  input  K,
  input  CLK,
  input  J,
  input  RESET,
  output Q,
  output INV_Q
);

  wire and_1_out, and_2_out, not_1_out, synchronized_rs_modified_1_inv_q, synchronized_rs_modified_1_q;

  and and_1 (and_1_out, Q, K);
  and and_2 (and_2_out, J, INV_Q);
  synchronized_rs_modified synchronized_rs_modified_1 (
    .R(and_1_out), .CLK(CLK), .S(and_2_out), .RESET(RESET), .Q(synchronized_rs_modified_1_q),
    .INV_Q(synchronized_rs_modified_1_inv_q));
  not not_1 (not_1_out, CLK);
  synchronized_rs_modified synchronized_rs_modified_2 (
    .R(synchronized_rs_modified_1_inv_q), .CLK(not_1_out), .S(synchronized_rs_modified_1_q), .RESET(RESET),
    .Q(Q), .INV_Q(INV_Q));
endmodule

module indicator (
  input  CLK,
  input  RESET,
  output [2:0] O_DATA
);

  wire and_1_out, not_1_out, or_1_out;

  or or_1 (or_1_out, RESET, and_1_out);
  not not_1 (not_1_out, O_DATA[1]);
  and and_1 (and_1_out, O_DATA[0], not_1_out, O_DATA[2]);
  jk_trigger jk_trigger_1 (.K(1'b1), .CLK(CLK), .J(1'b1), .RESET(or_1_out), .INV_Q(O_DATA[0]));  // open: Q
  jk_trigger jk_trigger_2 (.K(1'b1), .CLK(O_DATA[0]), .J(1'b1), .RESET(or_1_out), .INV_Q(O_DATA[1]));  // open: Q
  jk_trigger jk_trigger_3 (.K(1'b1), .CLK(O_DATA[1]), .J(1'b1), .RESET(or_1_out), .INV_Q(O_DATA[2]));  // open: Q
endmodule

module \checker  (
  input  AND_1,
  input  AND_2,
  input  OR_1,
  output RESULT
);

  wire and_1_out;

  and u_and_1 (and_1_out, AND_1, AND_2);
  or u_or_1 (RESULT, and_1_out, OR_1);
endmodule

module converter_minus (
  input  [2:0] I_DATA,
  output [2:0] O_DATA
);

  wire and_1_out, and_2_out, and_3_out, and_4_out, and_5_out, and_6_out, and_7_out, and_8_out, and_9_out,
       and_10_out, and_11_out, and_12_out, and_13_out, and_14_out, and_15_out, check_0_1_o_data,
       check_1_1_o_data, check_2_1_o_data, check_3_1_o_data, check_4_1_o_data, not_1_out, not_2_out,
       not_3_out, not_4_out, not_5_out, not_6_out, not_7_out, not_8_out, not_9_out, not_10_out;

  check_1 check_1_1 (.I_DATA(I_DATA), .O_DATA(check_1_1_o_data));
  check_2 check_2_1 (.I_DATA(I_DATA), .O_DATA(check_2_1_o_data));
  check_3 check_3_1 (.I_DATA(I_DATA), .O_DATA(check_3_1_o_data));
  check_4 check_4_1 (.I_DATA(I_DATA), .O_DATA(check_4_1_o_data));
  check_0 check_0_1 (.I_DATA(I_DATA), .O_DATA(check_0_1_o_data));
  not not_1 (not_1_out, 1'b1);
  not not_2 (not_2_out, 1'b1);
  not not_3 (not_3_out, 1'b1);
  not not_4 (not_4_out, 1'b1);
  not not_5 (not_5_out, 1'b1);
  not not_6 (not_6_out, 1'b1);
  not not_7 (not_7_out, 1'b1);
  not not_8 (not_8_out, 1'b1);
  not not_9 (not_9_out, 1'b1);
  not not_10 (not_10_out, 1'b1);
  and and_1 (and_1_out, not_1_out, check_1_1_o_data);
  and and_2 (and_2_out, not_2_out, check_1_1_o_data);
  and and_3 (and_3_out, not_3_out, check_1_1_o_data);
  and and_4 (and_4_out, 1'b1, check_2_1_o_data);
  and and_5 (and_5_out, not_4_out, check_2_1_o_data);
  and and_6 (and_6_out, not_5_out, check_2_1_o_data);
  and and_7 (and_7_out, not_6_out, check_3_1_o_data);
  and and_8 (and_8_out, 1'b1, check_3_1_o_data);
  and and_9 (and_9_out, not_7_out, check_3_1_o_data);
  and and_10 (and_10_out, 1'b1, check_4_1_o_data);
  and and_11 (and_11_out, 1'b1, check_4_1_o_data);
  and and_12 (and_12_out, not_8_out, check_4_1_o_data);
  and and_13 (and_13_out, not_9_out, check_0_1_o_data);
  and and_14 (and_14_out, not_10_out, check_0_1_o_data);
  and and_15 (and_15_out, 1'b1, check_0_1_o_data);
  or or_1 (O_DATA[0], and_1_out, and_4_out, and_7_out, and_10_out, and_13_out);
  or or_2 (O_DATA[1], and_2_out, and_8_out, and_5_out, and_11_out, and_14_out);
  or or_3 (O_DATA[2], and_3_out, and_6_out, and_9_out, and_12_out, and_15_out);
endmodule

module module_5 (
  input  [2:0] I_DATA,
  output [2:0] O_DATA
);

  wire and_1_out, and_2_out, and_3_out, and_4_out, and_5_out, and_6_out, and_7_out, and_8_out, and_9_out,
       and_10_out, and_11_out, and_12_out, and_13_out, and_14_out, and_15_out, and_16_out, and_17_out,
       and_18_out, check_0_1_o_data, check_1_1_o_data, check_2_1_o_data, check_3_1_o_data, check_4_1_o_data,
       not_1_out, not_2_out, not_3_out, not_4_out, not_5_out, not_6_out, not_7_out, not_8_out, not_9_out,
       not_10_out, not_11_out, not_12_out, or_1_out, or_2_out, or_3_out;

  not not_1 (not_1_out, I_DATA[1]);
  not not_2 (not_2_out, I_DATA[0]);
  check_0 check_0_1 (.I_DATA(I_DATA), .O_DATA(check_0_1_o_data));
  check_1 check_1_1 (.I_DATA(I_DATA), .O_DATA(check_1_1_o_data));
  check_2 check_2_1 (.I_DATA(I_DATA), .O_DATA(check_2_1_o_data));
  check_3 check_3_1 (.I_DATA(I_DATA), .O_DATA(check_3_1_o_data));
  check_4 check_4_1 (.I_DATA(I_DATA), .O_DATA(check_4_1_o_data));
  and and_1 (and_1_out, I_DATA[0], not_1_out, I_DATA[2]);
  and and_2 (and_2_out, not_2_out, I_DATA[1], I_DATA[2]);
  and and_3 (and_3_out, I_DATA[0], I_DATA[1], I_DATA[2]);
  or or_1 (or_1_out, and_1_out, check_0_1_o_data);
  or or_2 (or_2_out, and_2_out, check_1_1_o_data);
  or or_3 (or_3_out, and_3_out, check_2_1_o_data);
  not not_3 (not_3_out, 1'b1);
  not not_4 (not_4_out, 1'b1);
  not not_5 (not_5_out, 1'b1);
  not not_6 (not_6_out, 1'b1);
  not not_7 (not_7_out, 1'b1);
  not not_8 (not_8_out, 1'b1);
  not not_9 (not_9_out, 1'b1);
  not not_10 (not_10_out, 1'b1);
  not not_11 (not_11_out, 1'b1);
  not not_12 (not_12_out, 1'b1);
  and and_4 (and_4_out, not_3_out, or_1_out);
  and and_5 (and_5_out, not_4_out, or_1_out);
  and and_6 (and_6_out, not_5_out, or_1_out);
  and and_7 (and_7_out, 1'b1, or_2_out);
  and and_8 (and_8_out, not_6_out, or_2_out);
  and and_9 (and_9_out, not_7_out, or_2_out);
  and and_10 (and_10_out, not_8_out, or_3_out);
  and and_11 (and_11_out, 1'b1, or_3_out);
  and and_12 (and_12_out, not_9_out, or_3_out);
  and and_13 (and_13_out, 1'b1, check_3_1_o_data);
  and and_14 (and_14_out, 1'b1, check_3_1_o_data);
  and and_15 (and_15_out, not_10_out, check_3_1_o_data);
  and and_16 (and_16_out, not_11_out, check_4_1_o_data);
  and and_17 (and_17_out, not_12_out, check_4_1_o_data);
  and and_18 (and_18_out, 1'b1, check_4_1_o_data);
  or or_4 (O_DATA[0], and_4_out, and_7_out, and_10_out, and_13_out, and_16_out);
  or or_5 (O_DATA[1], and_5_out, and_11_out, and_8_out, and_14_out, and_17_out);
  or or_6 (O_DATA[2], and_6_out, and_9_out, and_12_out, and_15_out, and_18_out);
endmodule

module my_stack (
  input  [3:0] I_DATA,
  input  RESET,
  input  CLK,
  input  [1:0] COMMAND,
  input  [2:0] INDEX,
  output [3:0] O_DATA
);

  wire and_1_out, and_2_out, and_3_out, and_4_out, and_5_out, and_6_out, and_7_out, and_8_out,
       check_0_1_o_data, check_0_2_o_data, check_0_3_o_data, check_1_1_o_data, check_1_2_o_data,
       check_1_3_o_data, check_2_1_o_data, check_2_2_o_data, check_2_3_o_data, check_3_1_o_data,
       check_3_2_o_data, check_3_3_o_data, check_4_1_o_data, check_4_2_o_data, check_4_3_o_data,
       checker_1_result, checker_2_result, checker_3_result, checker_4_result, checker_5_result, not_1_out,
       not_2_out;
  wire [2:0] converter_1_o_data, converter_2_o_data, converter_minus_1_o_data, indicator_1_o_data,
       indicator_2_o_data, module_5_1_o_data;
  wire [3:0] mem_4_bits_1_o_data, mem_4_bits_2_o_data, mem_4_bits_3_o_data, mem_4_bits_4_o_data,
       mem_4_bits_5_o_data, new_and_1_result, new_and_2_result, new_and_3_result, new_and_4_result,
       new_and_5_result;

  module_5 module_5_1 (.I_DATA(INDEX), .O_DATA(module_5_1_o_data));
  not not_1 (not_1_out, COMMAND[1]);
  not not_2 (not_2_out, COMMAND[0]);
  converter converter_1 (
    .ELEMENT_1(converter_minus_1_o_data), .ELEMENT_2(module_5_1_o_data), .O_DATA(converter_1_o_data));
  indicator indicator_1 (.CLK(and_1_out), .RESET(RESET), .O_DATA(indicator_1_o_data));
  indicator indicator_2 (.CLK(and_2_out), .RESET(RESET), .O_DATA(indicator_2_o_data));
  converter converter_2 (.ELEMENT_1(indicator_1_o_data), .ELEMENT_2(indicator_2_o_data), .O_DATA(converter_2_o_data));
  converter_minus converter_minus_1 (.I_DATA(converter_2_o_data), .O_DATA(converter_minus_1_o_data));
  and and_1 (and_1_out, COMMAND[0], CLK, not_1_out);
  and and_2 (and_2_out, not_2_out, CLK, COMMAND[1]);
  and and_3 (and_3_out, COMMAND[0], CLK, COMMAND[1]);
  check_0 check_0_1 (.I_DATA(converter_1_o_data), .O_DATA(check_0_1_o_data));
  check_1 check_1_1 (.I_DATA(converter_1_o_data), .O_DATA(check_1_1_o_data));
  check_2 check_2_1 (.I_DATA(converter_1_o_data), .O_DATA(check_2_1_o_data));
  check_3 check_3_1 (.I_DATA(converter_1_o_data), .O_DATA(check_3_1_o_data));
  check_4 check_4_1 (.I_DATA(converter_1_o_data), .O_DATA(check_4_1_o_data));
  and and_4 (and_4_out, and_3_out, check_0_1_o_data);
  and and_5 (and_5_out, and_3_out, check_1_1_o_data);
  and and_6 (and_6_out, check_2_1_o_data, and_3_out);
  and and_7 (and_7_out, and_3_out, check_3_1_o_data);
  and and_8 (and_8_out, and_3_out, check_4_1_o_data);
  check_0 check_0_2 (.I_DATA(converter_2_o_data), .O_DATA(check_0_2_o_data));
  check_1 check_1_2 (.I_DATA(converter_2_o_data), .O_DATA(check_1_2_o_data));
  check_2 check_2_2 (.I_DATA(converter_2_o_data), .O_DATA(check_2_2_o_data));
  check_3 check_3_2 (.I_DATA(converter_2_o_data), .O_DATA(check_3_2_o_data));
  check_4 check_4_2 (.I_DATA(converter_2_o_data), .O_DATA(check_4_2_o_data));
  mem_4_bits mem_4_bits_1 (
    .RESET(RESET), .CLK(and_1_out), .KEY(check_0_2_o_data), .I_DATA(I_DATA), .O_DATA(mem_4_bits_1_o_data));
  check_0 check_0_3 (.I_DATA(converter_minus_1_o_data), .O_DATA(check_0_3_o_data));
  \checker  checker_1 (.AND_1(and_2_out), .AND_2(check_0_3_o_data), .OR_1(and_4_out), .RESULT(checker_1_result));
  mem_4_bits mem_4_bits_2 (
    .RESET(RESET), .CLK(and_1_out), .KEY(check_1_2_o_data), .I_DATA(I_DATA), .O_DATA(mem_4_bits_2_o_data));
  check_1 check_1_3 (.I_DATA(converter_minus_1_o_data), .O_DATA(check_1_3_o_data));
  \checker  checker_2 (.AND_1(check_1_3_o_data), .AND_2(and_2_out), .OR_1(and_5_out), .RESULT(checker_2_result));
  mem_4_bits mem_4_bits_3 (
    .RESET(RESET), .CLK(and_1_out), .KEY(check_2_2_o_data), .I_DATA(I_DATA), .O_DATA(mem_4_bits_3_o_data));
  check_2 check_2_3 (.I_DATA(converter_minus_1_o_data), .O_DATA(check_2_3_o_data));
  \checker  checker_3 (.AND_1(and_2_out), .AND_2(check_2_3_o_data), .OR_1(and_6_out), .RESULT(checker_3_result));
  mem_4_bits mem_4_bits_4 (
    .RESET(RESET), .CLK(and_1_out), .KEY(check_3_2_o_data), .I_DATA(I_DATA), .O_DATA(mem_4_bits_4_o_data));
  check_3 check_3_3 (.I_DATA(converter_minus_1_o_data), .O_DATA(check_3_3_o_data));
  \checker  checker_4 (.AND_1(and_2_out), .AND_2(check_3_3_o_data), .OR_1(and_7_out), .RESULT(checker_4_result));
  mem_4_bits mem_4_bits_5 (
    .RESET(RESET), .CLK(and_1_out), .KEY(check_4_2_o_data), .I_DATA(I_DATA), .O_DATA(mem_4_bits_5_o_data));
  check_4 check_4_3 (.I_DATA(converter_minus_1_o_data), .O_DATA(check_4_3_o_data));
  \checker  checker_5 (.AND_1(and_2_out), .AND_2(check_4_3_o_data), .OR_1(and_8_out), .RESULT(checker_5_result));
  new_and new_and_1 (.I_DATA(mem_4_bits_1_o_data), .KEY(checker_1_result), .RESULT(new_and_1_result));
  new_and new_and_2 (.I_DATA(mem_4_bits_2_o_data), .KEY(checker_2_result), .RESULT(new_and_2_result));
  new_and new_and_3 (.I_DATA(mem_4_bits_3_o_data), .KEY(checker_3_result), .RESULT(new_and_3_result));
  new_and new_and_4 (.I_DATA(mem_4_bits_4_o_data), .KEY(checker_4_result), .RESULT(new_and_4_result));
  new_and new_and_5 (.I_DATA(mem_4_bits_5_o_data), .KEY(checker_5_result), .RESULT(new_and_5_result));
  result result_1 (
    .A0(new_and_1_result), .A1(new_and_2_result), .A2(new_and_3_result), .A3(new_and_4_result),
    .A4(new_and_5_result), .res(O_DATA));
endmodule
